# Fritzing sketch schematic (saved by Fritzing 0.9.3b)
circuit board: 8.46667cm x 5.64444cm
breadboards: 1

parts:
  FTDI_board = FTDI Basic Programmer
  S2 = Round Pushbutton
  X1 = DB9 Connector [package=db9]
  X2 = DB9 Connector [package=db9]
  DHT2 = DHT11 Humitidy and Temperature Sensor
  BAT2 = Battery Holders [package=battcom_20mm_pth]
  U2 = ESP8266 WiFi Module [part_number=ESP8266]

nets:
  N1: FTDI_board.RXI, X1.2
  N2: FTDI_board.TXO, X1.3
  N3: FTDI_board.GND, X1.5
  GND: S2.leg0, X2.5, DHT2.GND, BAT2.-, U2.GND, U2.GPIO_15
  N4: S2.leg1, U2.GPIO_0
  N5: X2.2, U2.TXD
  N6: X2.3, U2.RXD
  N7: DHT2.VDD, U2.GPIO_5
  N8: DHT2.DATA, U2.GPIO_4
  N9: BAT2.+, U2.VCC, U2.CH_PD
  N10: U2.GPIO_16, U2.REST

custom parts:
  DHT11 Humitidy and Temperature Sensor: DHT11 Humidity and Temperature Sensor
  ESP8266 WiFi Module: Generic WiFi Module based on the ESP8266 with onboard PCB antenna and UART communications
