# Fritzing sketch schematic_plug (saved by Fritzing 0.9.3b)
breadboards: 1

parts:
  U1 = ESP8266 WiFi Module [part_number=ESP8266]
  J1 = Power Jack [package=power_jack_pth]
  S1 = Round Pushbutton
  RELAY1 = CAR RELAY [part_number=NVF4-2 package=THT]
  S2 = Round Pushbutton

nets:
  N1: U1.VCC, U1.CH_PD, J1.PWR
  N2: U1.GPIO_0, S1.leg0
  GND: U1.GND, U1.GPIO_15, J1.GND, RELAY1.86, S2.leg1
  N3: U1.GPIO_4, RELAY1.85
  N4: U1.GPIO_5, S2.leg0

custom parts:
  ESP8266 WiFi Module: Generic WiFi Module based on the ESP8266 with onboard PCB antenna and UART communications
